// Logisim project CPU.circ as structural Verilog: 4 circuits, main circuit main
module main (
);

  wire button_1_out, clock_1_out, uc_1_p3, uc_1_p6, uc_1_p7, uc_1_p8, uc_1_p10, uc_1_p11, uc_1_p12;
  wire [2:0] uc_1_p13;
  wire [3:0] alu_proc_1_out_6, multiplexer_1_out, pc_1_out, ram_1_data, regfile_1_p6, regfile_1_p7, uc_1_p4,
       uc_1_p9;
  wire [11:0] rom_1_data;

  // Probe on pc_1_out
  ROM #(.addrWidth(4), .dataWidth(12)) rom_1 (.addr(pc_1_out), .data(rom_1_data), .sel(1'b1));
  PC pc_1 (.in(uc_1_p4), .out(pc_1_out));
  // Probe on ram_1_data
  // Probe on rom_1_data
  // Probe on uc_1_p4
  Button button_1 (.out(button_1_out));
  // Probe on multiplexer_1_out
  Multiplexer #(.width(4), .enable("false")) multiplexer_1 (
    .in0(alu_proc_1_out_6), .in1(ram_1_data), .out(multiplexer_1_out), .sel(uc_1_p6));
  // Probe on uc_1_p7
  // Probe on uc_1_p8
  // Probe on uc_1_p10
  // UC uc_1: pin names not known; wires that end beside it: rom_1_data, pc_1_out, uc_1_p3, uc_1_p4, button_1_out, uc_1_p6, uc_1_p7, uc_1_p8, uc_1_p9, uc_1_p10, uc_1_p11, uc_1_p12, uc_1_p13
  // Probe on uc_1_p9
  // RegFile regfile_1: pin names not known; wires that end beside it: multiplexer_1_out, uc_1_p7, uc_1_p10, uc_1_p11, uc_1_p12, regfile_1_p6, regfile_1_p7
  // Probe on uc_1_p11
  // Probe on uc_1_p12
  Clock clock_1 (.out(clock_1_out));
  // Probe on uc_1_p13
  RAM #(.addrWidth(4), .dataWidth(4), .bus("separate")) ram_1 (
    .addr(uc_1_p9), .din(alu_proc_1_out_6), .data(ram_1_data), .str(uc_1_p8), .clk(clock_1_out), .ld(1'b1));  // open: sel, clr
  // Probe on regfile_1_p6
  // Probe on alu_proc_1_out_6
  // Probe on regfile_1_p7
  ALU_PROC alu_proc_1 (
    .Ci(1'b0), .S(uc_1_p13), .in_1(regfile_1_p6), .in_2(regfile_1_p7), .out_6(alu_proc_1_out_6));  // open: Co

  // Notes on the sheet:
  //   contents of rom_1 (hex, n*v repeats v):
  //   400 444 84 888 400 444 84 888 400 444 84 888 400 444 84 888
endmodule

module PC (
  input  [3:0] in,
  output [3:0] out
);

  REGISTER_4_bits register_4_bits_1 (.CLK(1'b1), .READ(1'b1), .D(in), .out_4(out));
endmodule

module Test (
  input  [3:0] in_1
);

  wire button_1_out;
  wire [3:0] pc_increase_1_out, register_4_bits_1_out_4;

  // Probe on register_4_bits_1_out_4
  Button button_1 (.out(button_1_out));
  PC_Increase pc_increase_1 (.in(register_4_bits_1_out_4), .RESET(button_1_out), .out(pc_increase_1_out));
  // Probe on pc_increase_1_out
  // Probe on register_4_bits_1_out_4
  REGISTER_4_bits register_4_bits_1 (.CLK(1'b1), .READ(1'b1), .D(pc_increase_1_out), .out_4(register_4_bits_1_out_4));
endmodule

module AD (
  input  [3:0] in,
  output [3:0] out
);

  REGISTER_4_bits register_4_bits_1 (.CLK(1'b1), .READ(1'b1), .D(in), .out_4(out));
endmodule
