// Logisim project CU.circ as structural Verilog: 1 circuit, main circuit main
// UC
module main (
  input  [11:0] In_in,
  output Read,
  output Write,
  output Source_Sel,
  output [1:0] RWrite_Sel,
  output [1:0] RX_Sel,
  output [1:0] RY_Sel
);
endmodule
